# Fritzing sketch wiring (saved by Fritzing 0.9.3b)
breadboards: 1

parts:
  U1 = NodeMCU V1.0
  R1 = Resistor [tolerance=±5% resistance=550 package=THT]
  R2 = Resistor [tolerance=±5% resistance=1k package=THT]
  R3 = Resistor [tolerance=±5% resistance=550 package=THT]
  R4 = Resistor [tolerance=±5% resistance=1k package=THT]
  Conn_8 = USB connector [package=THT]
  Conn_9 = USB connector [package=THT]

nets:
  N1: U1.D5, R1.Pin_1, R2.Pin_0
  N2: U1.D6, R3.Pin_1, R4.Pin_0
  N3: R1.Pin_0, Conn_8.GND
  N4: R2.Pin_1, Conn_8.5V
  N5: R3.Pin_0, Conn_9.GND
  N6: R4.Pin_1, Conn_9.5V

custom parts:
  NodeMCU V1.0: ESP8266 based NodeMCU
